# Fritzing sketch Dual-Channel-Voltage-Control-Circuit (saved by Fritzing 0.9.2b)
breadboards: 1

parts:
  Part2 = Adafruit MCP4725 Breakout Board - 12-Bit DAC [part_number="Adafruit #935"]
  Part3 = Adafruit MCP4725 Breakout Board - 12-Bit DAC [part_number="Adafruit #935"]
  Part1 = Arduino Uno (Rev3)

nets:
  VDD: Part2.VDD, Part3.VDD, Part3.A0, Part1.3V3
  GND: Part2.GND, Part3.GND, Part1.GND
  N1: Part2.SCL, Part3.SCL, Part1.A5/SCL
  N2: Part2.SDA, Part3.SDA, Part1.A4/SDA

custom parts:
  Adafruit MCP4725 Breakout Board - 12-Bit DAC: Your microcontroller probably has an ADC (analog -> digital converter) but does it have a DAC (digital -> analog converter)??? Now it can! This breakout board features the easy-to-use MCP4725 12-bit DAC. Control it via I2C and send it the value you want it to output, and the VOUT pin will have it. Great for audio / analog projects, such as when you can't use PWM but need a sine wave or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
