# Fritzing sketch Multiplexed-Voltage-Control-Circuit (saved by Fritzing 0.9.2b)
breadboards: 2

parts:
  Part2 = Adafruit MCP4725 Breakout Board - 12-Bit DAC [part_number="Adafruit #935"]
  Part3 = Adafruit MCP4725 Breakout Board - 12-Bit DAC [part_number="Adafruit #935"]
  Part1 = Arduino Uno (Rev3)
  Part4 = Adafruit TCA9548A
  Part5 = Adafruit MCP4725 Breakout Board - 12-Bit DAC [part_number="Adafruit #935"]  # not connected
  Part6 = Adafruit TCA9548A  # not connected
  Part7 = Adafruit MCP4725 Breakout Board - 12-Bit DAC [part_number="Adafruit #935"]  # not connected
  Part8 = Adafruit MCP4725 Breakout Board - 12-Bit DAC [part_number="Adafruit #935"]  # not connected
  Part9 = Adafruit MCP4725 Breakout Board - 12-Bit DAC [part_number="Adafruit #935"]  # not connected
  Part10 = Adafruit MCP4725 Breakout Board - 12-Bit DAC [part_number="Adafruit #935"]
  Part11 = Adafruit MCP4725 Breakout Board - 12-Bit DAC [part_number="Adafruit #935"]  # not connected

nets:
  VDD: Part2.VDD, Part3.VDD, Part1.5V, Part4.VCC, Part10.VDD
  GND: Part2.GND, Part3.GND, Part1.GND, Part4.GND, Part10.GND

custom parts:
  Adafruit MCP4725 Breakout Board - 12-Bit DAC: Your microcontroller probably has an ADC (analog -> digital converter) but does it have a DAC (digital -> analog converter)??? Now it can! This breakout board features the easy-to-use MCP4725 12-bit DAC. Control it via I2C and send it the value you want it to output, and the VOUT pin will have it. Great for audio / analog projects, such as when you can't use PWM but need a sine wave or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
  Adafruit TCA9548A: You just found the perfect I2C sensor, and you want to wire up two or three or more of them to your Arduino when you realize "Uh oh, this chip has a fixed I2C address, and from what I know about I2C, you cannot have two devices with the same address on the same SDA/SCL pins!" Are you out of luck? You would be, if you didn't have this ultra-cool TCA9548A 1-to-8 I2C multiplexer! Finally, a way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
